# Fritzing sketch Stepan3 (saved by Fritzing 0.9.2b)

parts:
  Part1 = Arduino Mega 2560 (Rev3)
  Arduino_CNC_Shield_V3_00_1 = Arduino_CNC_V3.00
  Part2 = SRF05 Ultrasonic Rangefinder
  U1 = ESP8266 WiFi Module [part_number=ESP8266]
  GY1 = MPU-6050 Board GY-521 [form="♀ (female)" package=THT]
  M3 = Stepper Motor - Bipolar
  M4 = Stepper Motor - Bipolar
  VCC1 = Battery
  VCC2 = Battery
  VCC3 = Battery
  R1 = Resistor [tolerance=±5% resistance=3.3k package=THT]
  R2 = Resistor [tolerance=±5% resistance=10k package=THT]
  IC1 = Voltage Regulator [package=to-220-alt]
  R3 = Resistor [tolerance=±5% resistance=1k package=THT]
  R4 = Resistor [tolerance=±5% resistance=2.2k package=THT]

nets:
  N1: Part1.A3, R1.Pin_1, R2.Pin_1
  N2: Part1.D21/SCL, GY1.pin3
  N3: Part1.D20/SDA, GY1.pin4
  N4: Part1.D19/RX1, Part2.Trig
  N5: Part1.D18/TX1, Part2.Echo
  N6: Part1.D15/RX3, U1.TXD
  N7: Part1.D14/TX3, R3.Pin_1
  N8: Part1.VIN, Arduino_CNC_Shield_V3_00_1.POWER_+, VCC3.+, R2.Pin_0
  N9: Part1.5V, GY1.pin1, IC1.OUT
  GND: Part1.GND, U1.GND, GY1.pin2, IC1.GND, R4.Pin_0
  N10: Arduino_CNC_Shield_V3_00_1.POWER_-, VCC1.-, R1.Pin_0
  N11: Arduino_CNC_Shield_V3_00_1.X-MTR_'1', M4.A
  N12: Arduino_CNC_Shield_V3_00_1.X-MTR_'2', M4.C
  N13: Arduino_CNC_Shield_V3_00_1.X-MTR_'3', M4.B
  N14: Arduino_CNC_Shield_V3_00_1.X-MTR_'4', M4.D
  N15: Arduino_CNC_Shield_V3_00_1.Y-MTR_'1', M3.A
  N16: Arduino_CNC_Shield_V3_00_1.Y-MTR_'2', M3.C
  N17: Arduino_CNC_Shield_V3_00_1.Y-MTR_'3', M3.B
  N18: Arduino_CNC_Shield_V3_00_1.Y-MTR_'4', M3.D
  5V: Arduino_CNC_Shield_V3_00_1.5V, Part2.VCC
  GND_2: Arduino_CNC_Shield_V3_00_1.GND, Part2.GND
  N19: U1.RXD, R3.Pin_0, R4.Pin_1
  N20: U1.VCC, U1.CH_PD, IC1.IN
  N21: VCC1.+, VCC2.-
  N22: VCC2.+, VCC3.-

notes:
  +9.6V hadrwired onCNC shield
  AMS1117

custom parts:
  Arduino_CNC_V3.00: Protoneer Arduino CNC Shield V3.00 If using Grbl V0.9: The “A” axis can not be used (yet). The “SCL” (Arduino A5) pin is now used for 'Probing' input. The “End Stops Z+ & Z-” (Arduino D11) and “SpnEn” (Arduino D12) have been switched!
  ESP8266 WiFi Module: Generic WiFi Module based on the ESP8266 with onboard PCB antenna and UART communications
  MPU-6050 Board GY-521: Acelerometro y Giroscopio MPU-6050 Board GY-521
